# Fritzing sketch Composite Video Colour #1.0 (saved by Fritzing 0.9.9b)
breadboards: 1

parts:
  Pico1 = Raspberry Pi Pico
  R1 = Resistor [tolerance=±5% resistance=680 power=0.25 package=THT]
  R2 = Resistor [tolerance=±5% resistance=680 power=0.25 package=THT]
  R3 = Resistor [tolerance=±5% resistance=680 power=0.25 package=THT]
  R6 = Resistor [tolerance=±5% resistance=270 power=0.25 package=THT]
  R7 = Resistor [tolerance=±5% resistance=270 power=0.25 package=THT]
  R8 = Resistor [tolerance=±5% resistance=270 power=0.25 package=THT]
  R11 = Resistor [tolerance=±5% resistance=100 power=0.25 package=THT]
  AD1 = AD724 [package="DIP (Dual Inline) [THT]"]
  R15 = Resistor [tolerance=±5% resistance=100 power=0.25 package=THT]
  R16 = Resistor [tolerance=±5% resistance=270 power=0.25 package=THT]
  R17 = Resistor [tolerance=±5% resistance=270 power=0.25 package=THT]
  R18 = Resistor [tolerance=±5% resistance=270 power=0.25 package=THT]
  R19 = Resistor [tolerance=±5% resistance=680 power=0.25 package=THT]
  R20 = Resistor [tolerance=±5% resistance=680 power=0.25 package=THT]
  R21 = Resistor [tolerance=±5% resistance=680 power=0.25 package=THT]
  R22 = Resistor [tolerance=±5% resistance=100 power=0.25 package=THT]
  R23 = Resistor [tolerance=±5% resistance=270 power=0.25 package=THT]
  R24 = Resistor [tolerance=±5% resistance=270 power=0.25 package=THT]
  R27 = Resistor [tolerance=±5% resistance=510 power=0.25 package=THT]
  R26 = Resistor [tolerance=±5% resistance=510 power=0.25 package=THT]
  XTAL1 = Crystal [frequency="4 MHz" package=THT]
  R29 = Resistor [tolerance=±5% resistance=75 power=0.25 package=THT]
  C2 = Ceramic Capacitor [capacitance=0.1µF voltage=6.3V package="100 mil [THT, multilayer]"]
  C3 = Ceramic Capacitor [capacitance=0.1µF voltage=6.3V package="100 mil [THT, multilayer]"]
  C1 = Ceramic Capacitor [capacitance=0.1µF voltage=6.3V package="100 mil [THT, multilayer]"]
  C4 = Electrolytic Capacitor [capacitance=220µF voltage=20V package="100 mil [THT, electrolytic]"]
  C5 = Electrolytic Capacitor [capacitance=10µF voltage=35V package="100 mil [THT, electrolytic]"]
  C6 = Ceramic Capacitor [capacitance=0.1µF voltage=35V package="100 mil [THT, multilayer]"]
  C7 = Electrolytic Capacitor [capacitance=10µF voltage=35V package="100 mil [THT, electrolytic]"]
  C8 = Ceramic Capacitor [capacitance=0.1µF voltage=35V package="100 mil [THT, multilayer]"]
  R30 = Resistor [tolerance=±5% power=0.25 resistance=2.2k package=THT]
  R31 = Resistor [tolerance=±5% power=0.25 resistance=3.3k package=THT]
  D1 = Schottky Diode [part_number=1N5817 package="Melf DO-213 AB [SMD]"]
  5VDC = Power plug

nets:
  5V: Pico1.VSYS, AD1.pin4, AD1.pin5, AD1.pin14, C5.+, C6.1, C7.+, C8.1, D1.cathode
  GND: Pico1.GND, R8.Pin_1, R11.Pin_1, AD1.pin1, AD1.pin2, AD1.pin12, AD1.pin13, R15.Pin_1, R16.Pin_1, R22.Pin_1, R23.Pin_1, XTAL1.pin_1, C5.-, C6.0, C7.-, C8.0, R31.Pin_1, 5VDC.GND
  N1: Pico1.GP13, R30.Pin_1, R31.Pin_0
  HSYNC: Pico1.GP9, AD1.pin16
  VSYNC: Pico1.GP8, AD1.pin15
  B1: Pico1.GP7, R27.Pin_0
  B0: Pico1.GP6, R26.Pin_0
  G2: Pico1.GP5, R21.Pin_0
  G1: Pico1.GP4, R20.Pin_0
  G0: Pico1.GP3, R19.Pin_0
  R2: Pico1.GP2, R1.Pin_0
  R1: Pico1.GP1, R2.Pin_0
  R0: Pico1.GP0, R3.Pin_0
  N2: R1.Pin_1, R6.Pin_0, R11.Pin_0, C1.0
  N3: R2.Pin_1, R6.Pin_1, R7.Pin_0
  N4: R3.Pin_1, R7.Pin_1, R8.Pin_0
  XTAL: AD1.pin3, XTAL1.pin_0
  RED: AD1.pin6, C1.1
  GREEN: AD1.pin7, C2.1
  BLUE: AD1.pin8, C3.1
  N5: AD1.pin10, C4.+
  N6: R15.Pin_0, R18.Pin_0, R21.Pin_1, C2.0
  N7: R16.Pin_0, R17.Pin_1, R19.Pin_1
  N8: R17.Pin_0, R18.Pin_1, R20.Pin_1
  N9: R22.Pin_0, R24.Pin_0, R27.Pin_1, C3.0
  N10: R23.Pin_0, R24.Pin_1, R26.Pin_1
  N11: R29.Pin_0, C4.-
  RX: R30.Pin_0
  N12: D1.anode, 5VDC.VCC

custom parts:
  Raspberry Pi Pico: Raspberry Pi Pico. Based around the RP2040 microcontroller the Pico is a low cost microcontroller device bringing Raspberry Pi quality, cost, and easy of use to the microcontroller space.
  AD724: NTSC/PAL encoder
