# Fritzing sketch Composite Video Mono #1.1 (saved by Fritzing 0.9.9b)
breadboards: 1

parts:
  Pico1 = Raspberry Pi Pico
  R1 = Resistor [tolerance=±5% resistance=440 power=0.25 package=THT]
  R2 = Resistor [tolerance=±5% resistance=440 power=0.25 package=THT]
  R3 = Resistor [tolerance=±5% resistance=440 power=0.25 package=THT]
  R4 = Resistor [tolerance=±5% resistance=440 power=0.25 package=THT]
  R5 = Resistor [tolerance=±5% resistance=440 power=0.25 package=THT]
  R6 = Resistor [tolerance=±5% resistance=220 power=0.25 package=THT]
  R7 = Resistor [tolerance=±5% resistance=220 power=0.25 package=THT]
  R8 = Resistor [tolerance=±5% resistance=220 power=0.25 package=THT]
  R9 = Resistor [tolerance=±5% resistance=220 power=0.25 package=THT]
  R10 = Resistor [tolerance=±5% resistance=220 power=0.25 package=THT]
  R11 = Resistor [tolerance=±5% resistance=110 power=0.25 package=THT]
  R12 = Resistor [tolerance=±5% power=0.25 resistance=2.2k package=THT]
  R13 = Resistor [tolerance=±5% power=0.25 resistance=3.3k package=THT]
  D1 = Schottky Diode [part_number=1N5817 package="Melf DO-213 AB [SMD]"]
  5VDC = Power plug

nets:
  N1: Pico1.VSYS, D1.cathode
  GND: Pico1.GND, R10.Pin_1, R11.Pin_1, R13.Pin_0, 5VDC.GND
  N2: Pico1.GP13, R12.Pin_0, R13.Pin_1
  N3: Pico1.GP4, R1.Pin_0
  N4: Pico1.GP3, R2.Pin_0
  N5: Pico1.GP2, R3.Pin_0
  N6: Pico1.GP1, R4.Pin_0
  N7: Pico1.GP0, R5.Pin_0
  N8: R1.Pin_1, R6.Pin_0, R11.Pin_0
  N9: R2.Pin_1, R6.Pin_1, R7.Pin_0
  N10: R3.Pin_1, R7.Pin_1, R8.Pin_0
  N11: R4.Pin_1, R8.Pin_1, R9.Pin_0
  N12: R5.Pin_1, R9.Pin_1, R10.Pin_0
  RX: R12.Pin_1
  N13: D1.anode, 5VDC.VCC

custom parts:
  Raspberry Pi Pico: Raspberry Pi Pico. Based around the RP2040 microcontroller the Pico is a low cost microcontroller device bringing Raspberry Pi quality, cost, and easy of use to the microcontroller space.
